# Fritzing sketch proje_şema (saved by Fritzing 0.9.3b)

parts:
  Load_Cell1 = Load Cell - Red/white/black/green
  Part2 = HX711 Weighing Sensor Module
  Load_Cell2 = Load Cell - Red/white/black/green

nets:
  N1: Load_Cell1.wire1, Part2.E+, Load_Cell2.wire1
  N2: Load_Cell1.wire2, Part2.E-, Load_Cell2.wire2
  N3: Load_Cell1.wire3, Part2.A+, Load_Cell2.wire3
  N4: Load_Cell1.wire4, Part2.A-, Load_Cell2.wire4

custom parts:
  Load Cell - Red/white/black/green: A rectangle load cell/weighting pressure Sensor with four wires - Red, white, black, green. Normally corresponding with E+, E-, A+, A- respectively.
